# Fritzing sketch circuit (saved by Fritzing 0.9.3b)

parts:
  Cane_is_On = smd LED [color="Green (555nm)" package="0603 [SMD]"]
  SP2 = SPEAKER [package=pcb_mount_speaker]
  IC2 = L293D [package=THT]
  Part4 = Power Cell LiPo Charger/Booster
  USB_MINI-B1 = USB Connectors [package=usb-a-h]
  USB_A1 = USB Connectors [package=usb-minib]
  On/Off = SWITCH-MOMENTARY-2 [package=tactile-switch-1101ne]
  Up = SWITCH-MOMENTARY-2 [package=tactile_switch_smd-2]
  Right = SWITCH-MOMENTARY-2 [package=tactile_switch_smd-2]
  Middle = SWITCH-MOMENTARY-2 [package=tactile_switch_smd-2]
  Left = SWITCH-MOMENTARY-2 [package=tactile_switch_smd-2]
  U4 = LIPO-2000mAh [package=lipo-2000]
  Part5 = Arduino Nano (Rev3.0) (ICSP)
  Proximity_Sensor = HC-SR04 Ultrasonic Distance Sensor
  Bluetooth = Bluetooth HC-05 Macho
  Left_Vibrator = Vibration Motor- ROB-08449 [package=vibe-motor-10mm]
  Right_Vibrator = Vibration Motor- ROB-08449 [package=vibe-motor-10mm]
  Down = SWITCH-MOMENTARY-2 [package=tactile_switch_smd-2]
  Sign_Light = smd LED [color="White (8000K)" package="0603 [SMD]"]
  Battery_Alert = smd LED [color="Red (633nm)" package="0603 [SMD]"]

nets:
  GND: Cane_is_On.cathode, SP2.-, IC2.0V, Part4.GND, USB_MINI-B1.GND, USB_A1.GND, Up.2, Right.2, Middle.2, Left.2, U4.-, Part5.GND, Proximity_Sensor.ECHO, Bluetooth.GND, Left_Vibrator.-, Right_Vibrator.-, Down.2, Sign_Light.cathode, Battery_Alert.cathode
  VCC: Cane_is_On.anode, IC2.Enable_1, IC2.+V, Part5.5V, Proximity_Sensor.VCC, Bluetooth.VCC
  N1: SP2.+, Part5.D11/MOSI
  N2: IC2.In_1, IC2.In_2, Part5.D5
  N3: IC2.Out_1_(_Controlled_by_Enable_1_), Left_Vibrator.+
  N4: IC2.Out_2_(_Controlled_by_Enable_1_), Right_Vibrator.+
  N5: Part4.VCC, USB_A1.D+, On/Off.1
  N6: Part4.5VIN, USB_MINI-B1.D+
  N7: Part4.PS, U4.+, Part5.A0
  N8: On/Off.2, Part5.VIN
  N9: Up.1, Part5.D12/MISO
  N10: Right.1, Part5.D6
  N11: Middle.1, Part5.D10
  N12: Left.1, Part5.D9
  N13: Part5.D2, Bluetooth.State
  N14: Part5.D3, Bluetooth.TXD
  N15: Part5.D4, Bluetooth.RXD
  N16: Part5.D7, Proximity_Sensor.TRIG
  N17: Part5.D8, Proximity_Sensor.GND
  N18: Part5.A7, Battery_Alert.anode
  N19: Part5.A1, Sign_Light.anode
  N20: Part5.D13/SCK, Down.1
